// Digital circuit ALU.dig as structural Verilog
module ALU (
  input  Ctrl_In,
  input  Ctrl_Out,
  input  Clk,
  input  [31:0] Data_In,
  input  Sel_A,
  input  Sel_B,
  input  Sel_SUM,
  input  Sel_DIF,
  input  Sel_LSH,
  input  Sel_RSH,
  input  Sel_AND,
  input  Sel_OR,
  input  Sel_XOR,
  input  Sel_NOT,
  input  Sel_GT,
  input  Sel_GTE,
  input  Sel_LT,
  input  Sel_LTE,
  output [31:0] Data_Out,
  output Data_Ready
);

  wire and_1_out, and_2_out, and_3_out, and_4_out, and_5_out, and_6_out, and_7_out, and_8_out, and_9_out,
       and_10_out, and_11_out, and_12_out, and_13_out, and_14_out, and_15_out, and_16_out, comparator_1_eq;
  wire [0:0] comparator_1_gt, comparator_1_lt, or_2_out, or_3_out;
  wire [31:0] add_1_s, and_17_out, barrelshifter_1_out, barrelshifter_2_out, multiplexer_1_out,
       multiplexer_2_out, multiplexer_3_out, multiplexer_4_out, multiplexer_5_out, multiplexer_6_out,
       multiplexer_7_out, multiplexer_8_out, multiplexer_9_out, multiplexer_10_out, multiplexer_11_out,
       multiplexer_12_out, multiplexer_13_out, not_1_out, or_1_out, register_1_q, register_2_q, sub_1_s,
       xor_1_out;

  and and_1 (and_1_out, Ctrl_In, Sel_A);
  and and_2 (and_2_out, Ctrl_Out, Sel_A);
  and and_3 (and_3_out, Ctrl_In, Sel_B);
  and and_4 (and_4_out, Ctrl_Out, Sel_B);
  and and_5 (and_5_out, Ctrl_Out, Sel_SUM);
  and and_6 (and_6_out, Ctrl_Out, Sel_DIF);
  and and_7 (and_7_out, Ctrl_Out, Sel_LSH);
  and and_8 (and_8_out, Ctrl_Out, Sel_RSH);
  and and_9 (and_9_out, Ctrl_Out, Sel_AND);
  and and_10 (and_10_out, Ctrl_Out, Sel_OR);
  and and_11 (and_11_out, Ctrl_Out, Sel_XOR);
  and and_12 (and_12_out, Ctrl_Out, Sel_NOT);
  and and_13 (and_13_out, Ctrl_Out, Sel_GT);
  and and_14 (and_14_out, Ctrl_Out, Sel_GTE);
  and and_15 (and_15_out, Ctrl_Out, Sel_LT);
  and and_16 (and_16_out, Ctrl_Out, Sel_LTE);
  Register #(.Bits(32)) register_1 (.D(Data_In), .C(Clk), .en(and_1_out), .Q(register_1_q));
  Register #(.Bits(32)) register_2 (.D(Data_In), .C(Clk), .en(and_3_out), .Q(register_2_q));
  Add #(.Bits(32)) add_1 (.a(register_1_q), .b(register_2_q), .c_i(1'b0), .s(add_1_s));  // open: c_o
  Sub #(.Bits(32)) sub_1 (.a(register_1_q), .b(register_2_q), .c_i(1'b0), .s(sub_1_s));  // open: c_o
  BarrelShifter #(.Bits(32), .barrelShifterMode("rotate")) barrelshifter_1 (
    .in(register_1_q), .shift(register_2_q[5:0]), .out(barrelshifter_1_out));
  BarrelShifter #(.Bits(32), .barrelShifterMode("rotate")) barrelshifter_2 (
    .in(register_1_q), .shift(register_2_q[5:0]), .out(barrelshifter_2_out));
  assign and_17_out = register_1_q & register_2_q;  // And and_17, 32 bits wide
  assign or_1_out = register_1_q | register_2_q;  // Or or_1, 32 bits wide
  assign xor_1_out = register_1_q ^ register_2_q;  // XOr xor_1, 32 bits wide
  assign not_1_out = ~register_1_q;  // Not not_1, 32 bits wide
  Comparator #(.Bits(32)) comparator_1 (
    .a(register_1_q), .b(register_2_q), .gt(comparator_1_gt[0]), .eq(comparator_1_eq), .lt(comparator_1_lt[0]));
  or or_2 (or_2_out[0], comparator_1_gt[0], comparator_1_eq);
  or or_3 (or_3_out[0], comparator_1_eq, comparator_1_lt[0]);
  Multiplexer #(.Bits(32)) multiplexer_1 (
    .sel(and_2_out), .in_0({32{1'b0}}), .in_1(register_1_q), .out(multiplexer_1_out));
  Multiplexer #(.Bits(32)) multiplexer_2 (
    .sel(and_4_out), .in_0(multiplexer_1_out), .in_1(register_2_q), .out(multiplexer_2_out));
  Multiplexer #(.Bits(32)) multiplexer_3 (
    .sel(and_5_out), .in_0(multiplexer_2_out), .in_1(add_1_s), .out(multiplexer_3_out));
  Multiplexer #(.Bits(32)) multiplexer_4 (
    .sel(and_6_out), .in_0(multiplexer_3_out), .in_1(sub_1_s), .out(multiplexer_4_out));
  Multiplexer #(.Bits(32)) multiplexer_5 (
    .sel(and_7_out), .in_0(multiplexer_4_out), .in_1(barrelshifter_1_out), .out(multiplexer_5_out));
  Multiplexer #(.Bits(32)) multiplexer_6 (
    .sel(and_8_out), .in_0(multiplexer_5_out), .in_1(barrelshifter_2_out), .out(multiplexer_6_out));
  Multiplexer #(.Bits(32)) multiplexer_7 (
    .sel(and_9_out), .in_0(multiplexer_6_out), .in_1(and_17_out), .out(multiplexer_7_out));
  Multiplexer #(.Bits(32)) multiplexer_8 (
    .sel(and_10_out), .in_0(multiplexer_7_out), .in_1(or_1_out), .out(multiplexer_8_out));
  Multiplexer #(.Bits(32)) multiplexer_9 (
    .sel(and_11_out), .in_0(multiplexer_8_out), .in_1(xor_1_out), .out(multiplexer_9_out));
  Multiplexer #(.Bits(32)) multiplexer_10 (
    .sel(and_12_out), .in_0(multiplexer_9_out), .in_1(not_1_out), .out(multiplexer_10_out));
  Multiplexer #(.Bits(32)) multiplexer_11 (
    .sel(and_13_out), .in_0(multiplexer_10_out), .in_1({{31{1'b0}}, comparator_1_gt[0]}),
    .out(multiplexer_11_out));
  Multiplexer #(.Bits(32)) multiplexer_12 (
    .sel(and_14_out), .in_0(multiplexer_11_out), .in_1({{31{1'b0}}, or_2_out[0]}), .out(multiplexer_12_out));
  Multiplexer #(.Bits(32)) multiplexer_13 (
    .sel(and_15_out), .in_0(multiplexer_12_out), .in_1({{31{1'b0}}, comparator_1_lt[0]}),
    .out(multiplexer_13_out));
  Multiplexer #(.Bits(32)) multiplexer_14 (
    .sel(and_16_out), .in_0(multiplexer_13_out), .in_1({{31{1'b0}}, or_3_out[0]}), .out(Data_Out));
  or or_4 (Data_Ready, and_2_out, and_4_out, and_5_out, and_6_out, and_7_out, and_8_out, and_9_out, and_10_out, and_11_out, and_12_out, and_13_out, and_14_out, and_15_out, and_16_out);
endmodule
