// Digital circuit ClockSelect.dig as structural Verilog
module ClockSelect (
  input  ManA,
  input  ManB,
  input  ManC,
  input  ManD,
  input  ClkA,
  input  ClkB,
  input  ClkC,
  input  ClkD,
  input  AutoA,
  input  AutoB,
  input  AutoC,
  input  AutoD,
  output DispA,
  output DispB,
  output DispC,
  output DispD,
  output Clk,
  output nClk,
  output [1:0] Num
);

  wire multiplexer_1_out, or_1_out, or_2_out, or_3_out, or_4_out, or_5_out, or_6_out, or_7_out, or_8_out;

  or or_1 (or_1_out, ManA, AutoA);
  or or_2 (or_2_out, ManB, AutoB);
  or or_3 (or_3_out, ManC, AutoC);
  or or_4 (or_4_out, ManD, AutoD);
  or or_5 (or_5_out, or_2_out, or_3_out, or_4_out);
  or or_6 (or_6_out, or_1_out, or_3_out, or_4_out);
  or or_7 (or_7_out, or_1_out, or_2_out, or_4_out);
  or or_8 (or_8_out, or_1_out, or_2_out, or_3_out);
  RS_FF_AS rs_ff_as_1 (.S(or_1_out), .R(or_5_out), .Q(DispA));  // open: nQ
  RS_FF_AS rs_ff_as_2 (.S(or_2_out), .R(or_6_out), .Q(DispB));  // open: nQ
  RS_FF_AS rs_ff_as_3 (.S(or_3_out), .R(or_7_out), .Q(DispC));  // open: nQ
  RS_FF_AS rs_ff_as_4 (.S(or_4_out), .R(or_8_out), .Q(DispD));  // open: nQ
  PriorityEncoder #(.Selector_Bits(2)) priorityencoder_1 (
    .in0(DispA), .in1(DispB), .in2(DispC), .in3(DispD), .num(Num));  // open: any
  Multiplexer #(.Selector_Bits(2)) multiplexer_1 (
    .sel(Num), .in_0(ClkA), .in_1(ClkB), .in_2(ClkC), .in_3(ClkD), .out(multiplexer_1_out));
  xor xor_1 (Clk, 1'b0, multiplexer_1_out);
  xor xor_2 (nClk, multiplexer_1_out, 1'b1);

  // Notes on the sheet:
  //   Num: Clock mode as number
endmodule
