// Digital circuit DeviceSelector.dig as structural Verilog
module DeviceSelector (
  input  [15:0] Addr_Prog,
  input  [15:0] Addr,
  input  In_Dev,
  input  Out_Dev,
  output In,
  output Out
);

  wire comparator_1_eq;

  Comparator #(.Bits(16)) comparator_1 (.a(Addr_Prog), .b(Addr), .eq(comparator_1_eq));  // open: gt, lt
  and and_1 (In, In_Dev, comparator_1_eq);
  and and_2 (Out, comparator_1_eq, Out_Dev);
endmodule
