// Digital circuit InstructionStepper.dig as structural Verilog
module InstructionStepper (
  input  Step,
  input  Clk,
  input  Rst,
  input  Done,
  output Clk_Out
);

  wire and_1_out, and_2_out, not_1_out, not_2_out, or_1_out, rs_ff_as_1_q, rs_ff_as_2_q, rs_ff_as_3_nq,
       rs_ff_as_3_q, rs_ff_as_4_q;

  RS_FF_AS rs_ff_as_1 (.S(not_1_out), .R(or_1_out), .Q(rs_ff_as_1_q));  // open: nQ
  RS_FF_AS rs_ff_as_2 (.S(not_2_out), .R(rs_ff_as_3_nq), .Q(rs_ff_as_2_q));  // open: nQ
  not not_1 (not_1_out, Step);
  not not_2 (not_2_out, Done);
  and and_1 (and_1_out, Step, rs_ff_as_1_q);
  and and_2 (and_2_out, Done, rs_ff_as_2_q);
  RS_FF_AS rs_ff_as_3 (.S(and_1_out), .R(or_1_out), .Q(rs_ff_as_3_q), .nQ(rs_ff_as_3_nq));
  RS_FF_AS rs_ff_as_4 (.S(and_2_out), .R(rs_ff_as_3_nq), .Q(rs_ff_as_4_q));  // open: nQ
  and and_3 (Clk_Out, Clk, rs_ff_as_3_q);
  or or_1 (or_1_out, rs_ff_as_4_q, Rst);
endmodule
