// Digital circuit MMP-1.dig as structural Verilog
module MMP_1 (
  input  _8Hz,
  input  _100Hz,
  input  _8Hz_2
);

  wire _8Hz_p1, _8Hz_p2, _100Hz_p1, _100Hz_p2, Addr_Dest, Addr_Src, Addr_Step, alu_1_data_ready, and_1_out,
       and_2_out, Clk, comparator_1_eq, demultiplexer_1_out_0, demultiplexer_1_out_1, demultiplexer_1_out_2,
       demultiplexer_1_out_3, deviceselector_1_in, deviceselector_1_out, deviceselector_2_in,
       deviceselector_2_out, deviceselector_3_in, deviceselector_3_out, deviceselector_4_in,
       deviceselector_4_out, deviceselector_5_in, deviceselector_5_out, Instruction_Step__8Hz_p1,
       Instruction_Step__8Hz_p2, instructionstepper_1_clk_out, nClk, not_1_out, not_2_out, nRst, or_2_out,
       Out_Dev, rangedeviceselector_1_in, rangedeviceselector_1_out, rangedeviceselector_2_in,
       rangedeviceselector_2_out, Res_out, Rst, Single_Step_p1, Single_Step_p2, Step_2_out, Step_Inc;
  wire [1:0] clockselect_1_num, counter_1_out, multiplexer_13_out;
  wire [3:0] DispA_q, DispA_q_2, DispA_q_3, DispA_q_4, DispA_q_5, DispA_q_6, DispA_q_7, DispA_q_8, DispB_q,
       DispB_q_2, DispB_q_3, DispB_q_4, DispB_q_5, DispB_q_6, DispB_q_7, DispB_q_8, matrixcontroller_1_index;
  wire [13:0] Addr_Match_out;
  wire [15:0] Addr, Dest, matrixcontroller_1_row0, matrixcontroller_1_row1, matrixcontroller_1_row2,
       matrixcontroller_1_row3, matrixcontroller_1_row4, matrixcontroller_1_row5, matrixcontroller_1_row6,
       matrixcontroller_1_row7, matrixcontroller_1_row8, matrixcontroller_1_row9, matrixcontroller_1_row10,
       matrixcontroller_1_row11, matrixcontroller_1_row12, matrixcontroller_1_row13,
       matrixcontroller_1_row14, matrixcontroller_1_row15, matrixcontroller_1_rowdata, multiplexer_2_out,
       multiplexer_3_out, multiplexer_13_out_3, PrgmStep, Src;
  wire [15:2] multiplexer_13_out_2;
  wire [31:0] alu_1_data_out, multiplexer_1_out, multiplexer_5_out, multiplexer_6_out, multiplexer_7_out,
       multiplexer_8_out, multiplexer_9_out, multiplexer_10_out, multiplexer_11_out, multiplexer_12_out,
       ramdualport_1_d, rom_1_d, Temp_q;

  Register #(.Bits(32)) Temp (
    .D({multiplexer_13_out_3, multiplexer_13_out_2, multiplexer_13_out}), .C(Clk), .en(Addr_Src), .Q(Temp_q));
  Register #(.Bits(16)) u_Src (.D(multiplexer_13_out_3), .C(Clk), .en(Addr_Step), .Q(Src));
  Register #(.Bits(16)) u_Dest (.D({multiplexer_13_out_2, multiplexer_13_out}), .C(Clk), .en(Addr_Step), .Q(Dest));
  Comparator #(.Bits(16)) comparator_1 (.a(Dest), .b({16{1'b1}}), .eq(comparator_1_eq));  // open: gt, lt
  and and_1 (and_1_out, Addr_Dest, comparator_1_eq);
  CounterPreset #(.Bits(16)) Step (
    .en(and_2_out), .C(Clk), .dir(1'b0), .in({multiplexer_13_out_2, multiplexer_13_out}), .ld(and_1_out),
    .clr(Rst), .out(PrgmStep));  // open: ovf
  Button Res (.out(Res_out));
  Counter #(.Bits(2)) counter_1 (.en(1'b1), .C(nClk), .clr(Rst), .out(counter_1_out));  // open: ovf
  and and_2 (and_2_out, Step_Inc, not_1_out);
  ResetTimer resettimer_1 (.Rst_Raw(Res_out), .Clk(Clk), .nClk(nClk), .Rst(Rst), .nRst(nRst));
  Decoder #(.Selector_Bits(2)) decoder_1 (
    .sel(counter_1_out), .out_0(Addr_Step), .out_1(Addr_Src), .out_2(Addr_Dest), .out_3(Step_Inc));
  LED Load_Pointers (.in(Addr_Step));
  LED Read_Source (.in(Addr_Src));
  LED Write_Destination (.in(Addr_Dest));
  LED Increment_Step (.in(Step_Inc));
  or or_1 (Out_Dev, Addr_Step, Addr_Src);
  Multiplexer #(.Bits(32)) multiplexer_1 (.sel(Addr_Dest), .in_0({32{1'b0}}), .in_1(Temp_q), .out(multiplexer_1_out));
  not not_1 (not_1_out, comparator_1_eq);
  Multiplexer #(.Bits(16)) multiplexer_2 (.sel(Addr_Src), .in_0({16{1'b0}}), .in_1(Src), .out(multiplexer_2_out));
  Multiplexer #(.Bits(16)) multiplexer_3 (
    .sel(Addr_Dest), .in_0(multiplexer_2_out), .in_1(Dest), .out(multiplexer_3_out));
  Multiplexer #(.Bits(16)) multiplexer_4 (.sel(Addr_Step), .in_0(multiplexer_3_out), .in_1(PrgmStep), .out(Addr));
  or or_2 (or_2_out, not_2_out, Rst);
  DeviceSelector deviceselector_1 (
    .Addr_Prog(16'hfff0), .Addr(Addr), .In_Dev(Addr_Dest), .Out_Dev(Out_Dev), .In(deviceselector_1_in),
    .Out(deviceselector_1_out));
  RangeDeviceSelector rangedeviceselector_1 (
    .Addr_Upper(16'h3fff), .Addr_Lower({16{1'b0}}), .Addr(Addr), .In_Dev(Addr_Dest), .Out_Dev(Out_Dev),
    .In(rangedeviceselector_1_in), .Out(rangedeviceselector_1_out));
  RangeDeviceSelector rangedeviceselector_2 (
    .Addr_Upper(16'h7fff), .Addr_Lower(16'h4000), .Addr(Addr), .In_Dev(Addr_Dest), .Out_Dev(Out_Dev),
    .In(rangedeviceselector_2_in), .Out(rangedeviceselector_2_out));
  // Probe Program Step on PrgmStep
  Button Step_2 (.out(Step_2_out));
  InstructionStepper instructionstepper_1 (
    .Step(Step_2_out), .Clk(_8Hz_2), .Rst(or_2_out), .Done(Addr_Src), .Clk_Out(instructionstepper_1_clk_out));
  LED ErrROMWrite (.in(rangedeviceselector_1_in));
  // ButtonLED Single_Step: pin names not known; wires that end beside it: Single_Step_p1, Single_Step_p2
  // ButtonLED Instruction_Step__8Hz: pin names not known; wires that end beside it: Instruction_Step__8Hz_p1, Instruction_Step__8Hz_p2
  // ButtonLED _8Hz: pin names not known; wires that end beside it: _8Hz_p1, _8Hz_p2
  // ButtonLED _100Hz: pin names not known; wires that end beside it: _100Hz_p1, _100Hz_p2
  // Probe Address on Addr
  // Probe Bus on {multiplexer_13_out_3, multiplexer_13_out_2, multiplexer_13_out}
  not not_2 (not_2_out, Instruction_Step__8Hz_p2);
  ClockSelect clockselect_1 (
    .ManA(Single_Step_p1), .ManB(Instruction_Step__8Hz_p1), .ManC(_8Hz_p1), .ManD(_100Hz_p1),
    .ClkA(Step_2_out), .ClkB(instructionstepper_1_clk_out), .ClkC(_8Hz), .ClkD(_100Hz),
    .AutoA(demultiplexer_1_out_0), .AutoB(demultiplexer_1_out_1), .AutoC(demultiplexer_1_out_2),
    .AutoD(demultiplexer_1_out_3), .DispA(Single_Step_p2), .DispB(Instruction_Step__8Hz_p2), .DispC(_8Hz_p2),
    .DispD(_100Hz_p2), .Clk(Clk), .nClk(nClk), .Num(clockselect_1_num));
  Demultiplexer #(.Selector_Bits(2)) demultiplexer_1 (
    .sel(multiplexer_13_out), .in(deviceselector_1_in), .out_0(demultiplexer_1_out_0),
    .out_1(demultiplexer_1_out_1), .out_2(demultiplexer_1_out_2), .out_3(demultiplexer_1_out_3));
  // Probe Source on Src
  // Probe Destination on Dest
  ROM #(.bigEndian("true"), .AddrBits(14), .Bits(32)) rom_1 (.A(Addr[13:0]), .sel(1'b1), .D(rom_1_d));
  RAMDualPort #(.AddrBits(14), .Bits(32)) ramdualport_1 (
    .A(Addr[13:0]), .Din({multiplexer_13_out_3, multiplexer_13_out_2, multiplexer_13_out}),
    .str(rangedeviceselector_2_in), .C(Clk), .ld(1'b1), .D(ramdualport_1_d));
  // Probe on clockselect_1_num
  Multiplexer #(.Bits(32)) multiplexer_5 (
    .sel(deviceselector_1_out), .in_0(multiplexer_1_out), .in_1({{30{1'b0}}, clockselect_1_num}),
    .out(multiplexer_5_out));
  Multiplexer #(.Bits(32)) multiplexer_6 (
    .sel(rangedeviceselector_1_out), .in_0(multiplexer_5_out), .in_1(rom_1_d), .out(multiplexer_6_out));
  Multiplexer #(.Bits(32)) multiplexer_7 (
    .sel(rangedeviceselector_2_out), .in_0(multiplexer_6_out), .in_1(ramdualport_1_d), .out(multiplexer_7_out));
  DeviceSelector deviceselector_2 (
    .Addr_Prog(16'hf100), .Addr(Addr), .In_Dev(Addr_Dest), .Out_Dev(Out_Dev), .In(deviceselector_2_in),
    .Out(deviceselector_2_out));
  DeviceSelector deviceselector_3 (
    .Addr_Prog(16'hf101), .Addr(Addr), .In_Dev(Addr_Dest), .Out_Dev(Out_Dev), .In(deviceselector_3_in),
    .Out(deviceselector_3_out));
  DeviceSelector deviceselector_4 (
    .Addr_Prog(16'hf200), .Addr(Addr), .In_Dev(Addr_Dest), .Out_Dev(Out_Dev), .In(deviceselector_4_in),
    .Out(deviceselector_4_out));
  DeviceSelector deviceselector_5 (
    .Addr_Prog(16'hf201), .Addr(Addr), .In_Dev(Addr_Dest), .Out_Dev(Out_Dev), .In(deviceselector_5_in),
    .Out(deviceselector_5_out));
  LookUpTable #(.Bits(14)) Addr_Match (
    .in0(Addr[0]), .in1(Addr[1]), .in2(Addr[2]), .in3(Addr[3]), .in4(Addr[4]), .in5(Addr[5]), .in6(Addr[6]),
    .in7(Addr[7]), .in8(Addr[8]), .in9(Addr[9]), .in10(Addr[10]), .in11(Addr[11]), .in12(Addr[12]),
    .in13(Addr[13]), .in14(Addr[14]), .in15(Addr[15]), .out(Addr_Match_out));
  Register #(.Bits(32)) DispA (
    .D({multiplexer_13_out_3, multiplexer_13_out_2, multiplexer_13_out}), .C(Clk), .en(deviceselector_2_in),
    .Q({DispA_q_8, DispA_q_7, DispA_q_6, DispA_q_5, DispA_q_4, DispA_q_3, DispA_q_2, DispA_q}));
  Register #(.Bits(32)) DispB (
    .D({multiplexer_13_out_3, multiplexer_13_out_2, multiplexer_13_out}), .C(Clk), .en(deviceselector_3_in),
    .Q({DispB_q_8, DispB_q_7, DispB_q_6, DispB_q_5, DispB_q_4, DispB_q_3, DispB_q_2, DispB_q}));
  ALU alu_1 (
    .Ctrl_In(Addr_Dest), .Ctrl_Out(Out_Dev), .Clk(Clk),
    .Data_In({multiplexer_13_out_3, multiplexer_13_out_2, multiplexer_13_out}), .Sel_A(Addr_Match_out[0]),
    .Sel_B(Addr_Match_out[1]), .Sel_SUM(Addr_Match_out[2]), .Sel_DIF(Addr_Match_out[3]),
    .Sel_LSH(Addr_Match_out[4]), .Sel_RSH(Addr_Match_out[5]), .Sel_AND(Addr_Match_out[6]),
    .Sel_OR(Addr_Match_out[7]), .Sel_XOR(Addr_Match_out[8]), .Sel_NOT(Addr_Match_out[9]),
    .Sel_GT(Addr_Match_out[10]), .Sel_GTE(Addr_Match_out[11]), .Sel_LT(Addr_Match_out[12]),
    .Sel_LTE(Addr_Match_out[13]), .Data_Out(alu_1_data_out), .Data_Ready(alu_1_data_ready));
  Multiplexer #(.Bits(32)) multiplexer_8 (
    .sel(deviceselector_2_out), .in_0(multiplexer_7_out),
    .in_1({DispA_q_8, DispA_q_7, DispA_q_6, DispA_q_5, DispA_q_4, DispA_q_3, DispA_q_2, DispA_q}),
    .out(multiplexer_8_out));
  Multiplexer #(.Bits(32)) multiplexer_9 (
    .sel(deviceselector_3_out), .in_0(multiplexer_8_out),
    .in_1({DispB_q_8, DispB_q_7, DispB_q_6, DispB_q_5, DispB_q_4, DispB_q_3, DispB_q_2, DispB_q}),
    .out(multiplexer_9_out));
  Multiplexer #(.Bits(32)) multiplexer_10 (
    .sel(deviceselector_4_out), .in_0(multiplexer_9_out), .in_1({{28{1'b0}}, matrixcontroller_1_index}),
    .out(multiplexer_10_out));
  Multiplexer #(.Bits(32)) multiplexer_11 (
    .sel(deviceselector_5_out), .in_0(multiplexer_10_out), .in_1({{16{1'b0}}, matrixcontroller_1_rowdata}),
    .out(multiplexer_11_out));
  Multiplexer #(.Bits(32)) multiplexer_12 (
    .sel(alu_1_data_ready), .in_0(multiplexer_11_out), .in_1(alu_1_data_out), .out(multiplexer_12_out));
  Multiplexer #(.Bits(32)) multiplexer_13 (
    .sel(Rst), .in_0(multiplexer_12_out), .in_1({32{1'b0}}),
    .out({multiplexer_13_out_3, multiplexer_13_out_2, multiplexer_13_out}));
  MatrixController matrixcontroller_1 (
    .Clk(Clk), .W_Row(deviceselector_4_in), .W_Index(deviceselector_5_in),
    .Data({multiplexer_13_out_2, multiplexer_13_out}), .Row15(matrixcontroller_1_row15),
    .Row14(matrixcontroller_1_row14), .Row13(matrixcontroller_1_row13), .Row12(matrixcontroller_1_row12),
    .Row11(matrixcontroller_1_row11), .Row10(matrixcontroller_1_row10), .Row9(matrixcontroller_1_row9),
    .Row8(matrixcontroller_1_row8), .Row7(matrixcontroller_1_row7), .Row6(matrixcontroller_1_row6),
    .Row5(matrixcontroller_1_row5), .Row4(matrixcontroller_1_row4), .Row3(matrixcontroller_1_row3),
    .Row2(matrixcontroller_1_row2), .Row1(matrixcontroller_1_row1), .Row0(matrixcontroller_1_row0),
    .RowData(matrixcontroller_1_rowdata), .Index(matrixcontroller_1_index));
  Seven_Seg_Hex seven_seg_hex_1 (.d(DispA_q_8), .dp(1'b0));
  Seven_Seg_Hex seven_seg_hex_2 (.d(DispA_q_7), .dp(1'b0));
  Seven_Seg_Hex seven_seg_hex_3 (.d(DispB_q_8), .dp(1'b0));
  Seven_Seg_Hex seven_seg_hex_4 (.d(DispB_q_7), .dp(1'b0));
  LED led_1 (.in(matrixcontroller_1_row15[0]));
  LED led_2 (.in(matrixcontroller_1_row14[0]));
  LED led_3 (.in(matrixcontroller_1_row13[0]));
  LED led_4 (.in(matrixcontroller_1_row12[0]));
  LED led_5 (.in(matrixcontroller_1_row11[0]));
  LED led_6 (.in(matrixcontroller_1_row10[0]));
  LED led_7 (.in(matrixcontroller_1_row9[0]));
  LED led_8 (.in(matrixcontroller_1_row8[0]));
  LED led_9 (.in(matrixcontroller_1_row7[0]));
  LED led_10 (.in(matrixcontroller_1_row6[0]));
  LED led_11 (.in(matrixcontroller_1_row5[0]));
  LED led_12 (.in(matrixcontroller_1_row4[0]));
  LED led_13 (.in(matrixcontroller_1_row3[0]));
  LED led_14 (.in(matrixcontroller_1_row2[0]));
  LED led_15 (.in(matrixcontroller_1_row1[0]));
  LED led_16 (.in(matrixcontroller_1_row0[0]));
  Seven_Seg_Hex seven_seg_hex_5 (.d(DispA_q_6), .dp(1'b0));
  Seven_Seg_Hex seven_seg_hex_6 (.d(DispB_q_6), .dp(1'b0));
  LED led_17 (.in(matrixcontroller_1_row15[2]));
  LED led_18 (.in(matrixcontroller_1_row15[1]));
  LED led_19 (.in(matrixcontroller_1_row14[2]));
  LED led_20 (.in(matrixcontroller_1_row14[1]));
  LED led_21 (.in(matrixcontroller_1_row13[2]));
  LED led_22 (.in(matrixcontroller_1_row13[1]));
  LED led_23 (.in(matrixcontroller_1_row12[2]));
  LED led_24 (.in(matrixcontroller_1_row12[1]));
  LED led_25 (.in(matrixcontroller_1_row11[2]));
  LED led_26 (.in(matrixcontroller_1_row11[1]));
  LED led_27 (.in(matrixcontroller_1_row10[2]));
  LED led_28 (.in(matrixcontroller_1_row10[1]));
  LED led_29 (.in(matrixcontroller_1_row9[2]));
  LED led_30 (.in(matrixcontroller_1_row9[1]));
  LED led_31 (.in(matrixcontroller_1_row8[2]));
  LED led_32 (.in(matrixcontroller_1_row8[1]));
  LED led_33 (.in(matrixcontroller_1_row7[2]));
  LED led_34 (.in(matrixcontroller_1_row7[1]));
  LED led_35 (.in(matrixcontroller_1_row6[2]));
  LED led_36 (.in(matrixcontroller_1_row6[1]));
  LED led_37 (.in(matrixcontroller_1_row5[2]));
  LED led_38 (.in(matrixcontroller_1_row5[1]));
  LED led_39 (.in(matrixcontroller_1_row4[2]));
  LED led_40 (.in(matrixcontroller_1_row4[1]));
  LED led_41 (.in(matrixcontroller_1_row3[2]));
  LED led_42 (.in(matrixcontroller_1_row3[1]));
  LED led_43 (.in(matrixcontroller_1_row2[2]));
  LED led_44 (.in(matrixcontroller_1_row2[1]));
  LED led_45 (.in(matrixcontroller_1_row1[2]));
  LED led_46 (.in(matrixcontroller_1_row1[1]));
  LED led_47 (.in(matrixcontroller_1_row0[2]));
  LED led_48 (.in(matrixcontroller_1_row0[1]));
  Seven_Seg_Hex seven_seg_hex_7 (.d(DispA_q_5), .dp(1'b0));
  Seven_Seg_Hex seven_seg_hex_8 (.d(DispB_q_5), .dp(1'b0));
  LED led_49 (.in(matrixcontroller_1_row15[3]));
  LED led_50 (.in(matrixcontroller_1_row15[4]));
  LED led_51 (.in(matrixcontroller_1_row14[3]));
  LED led_52 (.in(matrixcontroller_1_row14[4]));
  LED led_53 (.in(matrixcontroller_1_row13[3]));
  LED led_54 (.in(matrixcontroller_1_row13[4]));
  LED led_55 (.in(matrixcontroller_1_row12[3]));
  LED led_56 (.in(matrixcontroller_1_row12[4]));
  LED led_57 (.in(matrixcontroller_1_row11[3]));
  LED led_58 (.in(matrixcontroller_1_row11[4]));
  LED led_59 (.in(matrixcontroller_1_row10[3]));
  LED led_60 (.in(matrixcontroller_1_row10[4]));
  LED led_61 (.in(matrixcontroller_1_row9[3]));
  LED led_62 (.in(matrixcontroller_1_row9[4]));
  LED led_63 (.in(matrixcontroller_1_row8[3]));
  LED led_64 (.in(matrixcontroller_1_row8[4]));
  LED led_65 (.in(matrixcontroller_1_row7[3]));
  LED led_66 (.in(matrixcontroller_1_row7[4]));
  LED led_67 (.in(matrixcontroller_1_row6[3]));
  LED led_68 (.in(matrixcontroller_1_row6[4]));
  LED led_69 (.in(matrixcontroller_1_row5[3]));
  LED led_70 (.in(matrixcontroller_1_row5[4]));
  LED led_71 (.in(matrixcontroller_1_row4[3]));
  LED led_72 (.in(matrixcontroller_1_row4[4]));
  LED led_73 (.in(matrixcontroller_1_row3[3]));
  LED led_74 (.in(matrixcontroller_1_row3[4]));
  LED led_75 (.in(matrixcontroller_1_row2[3]));
  LED led_76 (.in(matrixcontroller_1_row2[4]));
  LED led_77 (.in(matrixcontroller_1_row1[3]));
  LED led_78 (.in(matrixcontroller_1_row1[4]));
  LED led_79 (.in(matrixcontroller_1_row0[3]));
  LED led_80 (.in(matrixcontroller_1_row0[4]));
  Seven_Seg_Hex seven_seg_hex_9 (.d(DispA_q_4), .dp(1'b0));
  Seven_Seg_Hex seven_seg_hex_10 (.d(DispA_q_3), .dp(1'b0));
  Seven_Seg_Hex seven_seg_hex_11 (.d(DispB_q_4), .dp(1'b0));
  Seven_Seg_Hex seven_seg_hex_12 (.d(DispB_q_3), .dp(1'b0));
  LED led_81 (.in(matrixcontroller_1_row15[6]));
  LED led_82 (.in(matrixcontroller_1_row15[5]));
  LED led_83 (.in(matrixcontroller_1_row14[6]));
  LED led_84 (.in(matrixcontroller_1_row14[5]));
  LED led_85 (.in(matrixcontroller_1_row13[6]));
  LED led_86 (.in(matrixcontroller_1_row13[5]));
  LED led_87 (.in(matrixcontroller_1_row12[6]));
  LED led_88 (.in(matrixcontroller_1_row12[5]));
  LED led_89 (.in(matrixcontroller_1_row11[6]));
  LED led_90 (.in(matrixcontroller_1_row11[5]));
  LED led_91 (.in(matrixcontroller_1_row10[6]));
  LED led_92 (.in(matrixcontroller_1_row10[5]));
  LED led_93 (.in(matrixcontroller_1_row9[6]));
  LED led_94 (.in(matrixcontroller_1_row9[5]));
  LED led_95 (.in(matrixcontroller_1_row8[6]));
  LED led_96 (.in(matrixcontroller_1_row8[5]));
  LED led_97 (.in(matrixcontroller_1_row7[6]));
  LED led_98 (.in(matrixcontroller_1_row7[5]));
  LED led_99 (.in(matrixcontroller_1_row6[6]));
  LED led_100 (.in(matrixcontroller_1_row6[5]));
  LED led_101 (.in(matrixcontroller_1_row5[6]));
  LED led_102 (.in(matrixcontroller_1_row5[5]));
  LED led_103 (.in(matrixcontroller_1_row4[6]));
  LED led_104 (.in(matrixcontroller_1_row4[5]));
  LED led_105 (.in(matrixcontroller_1_row3[6]));
  LED led_106 (.in(matrixcontroller_1_row3[5]));
  LED led_107 (.in(matrixcontroller_1_row2[6]));
  LED led_108 (.in(matrixcontroller_1_row2[5]));
  LED led_109 (.in(matrixcontroller_1_row1[6]));
  LED led_110 (.in(matrixcontroller_1_row1[5]));
  LED led_111 (.in(matrixcontroller_1_row0[6]));
  LED led_112 (.in(matrixcontroller_1_row0[5]));
  Seven_Seg_Hex seven_seg_hex_13 (.d(DispA_q_2), .dp(1'b0));
  Seven_Seg_Hex seven_seg_hex_14 (.d(DispB_q_2), .dp(1'b0));
  LED led_113 (.in(matrixcontroller_1_row15[7]));
  LED led_114 (.in(matrixcontroller_1_row15[8]));
  LED led_115 (.in(matrixcontroller_1_row14[7]));
  LED led_116 (.in(matrixcontroller_1_row14[8]));
  LED led_117 (.in(matrixcontroller_1_row13[7]));
  LED led_118 (.in(matrixcontroller_1_row13[8]));
  LED led_119 (.in(matrixcontroller_1_row12[7]));
  LED led_120 (.in(matrixcontroller_1_row12[8]));
  LED led_121 (.in(matrixcontroller_1_row11[7]));
  LED led_122 (.in(matrixcontroller_1_row11[8]));
  LED led_123 (.in(matrixcontroller_1_row10[7]));
  LED led_124 (.in(matrixcontroller_1_row10[8]));
  LED led_125 (.in(matrixcontroller_1_row9[7]));
  LED led_126 (.in(matrixcontroller_1_row9[8]));
  LED led_127 (.in(matrixcontroller_1_row8[7]));
  LED led_128 (.in(matrixcontroller_1_row8[8]));
  LED led_129 (.in(matrixcontroller_1_row7[7]));
  LED led_130 (.in(matrixcontroller_1_row7[8]));
  LED led_131 (.in(matrixcontroller_1_row6[7]));
  LED led_132 (.in(matrixcontroller_1_row6[8]));
  LED led_133 (.in(matrixcontroller_1_row5[7]));
  LED led_134 (.in(matrixcontroller_1_row5[8]));
  LED led_135 (.in(matrixcontroller_1_row4[7]));
  LED led_136 (.in(matrixcontroller_1_row4[8]));
  LED led_137 (.in(matrixcontroller_1_row3[7]));
  LED led_138 (.in(matrixcontroller_1_row3[8]));
  LED led_139 (.in(matrixcontroller_1_row2[7]));
  LED led_140 (.in(matrixcontroller_1_row2[8]));
  LED led_141 (.in(matrixcontroller_1_row1[7]));
  LED led_142 (.in(matrixcontroller_1_row1[8]));
  LED led_143 (.in(matrixcontroller_1_row0[7]));
  LED led_144 (.in(matrixcontroller_1_row0[8]));
  Seven_Seg_Hex seven_seg_hex_15 (.d(DispA_q), .dp(1'b0));
  Seven_Seg_Hex seven_seg_hex_16 (.d(DispB_q), .dp(1'b0));
  LED led_145 (.in(matrixcontroller_1_row15[10]));
  LED led_146 (.in(matrixcontroller_1_row15[9]));
  LED led_147 (.in(matrixcontroller_1_row14[10]));
  LED led_148 (.in(matrixcontroller_1_row14[9]));
  LED led_149 (.in(matrixcontroller_1_row13[10]));
  LED led_150 (.in(matrixcontroller_1_row13[9]));
  LED led_151 (.in(matrixcontroller_1_row12[10]));
  LED led_152 (.in(matrixcontroller_1_row12[9]));
  LED led_153 (.in(matrixcontroller_1_row11[10]));
  LED led_154 (.in(matrixcontroller_1_row11[9]));
  LED led_155 (.in(matrixcontroller_1_row10[10]));
  LED led_156 (.in(matrixcontroller_1_row10[9]));
  LED led_157 (.in(matrixcontroller_1_row9[10]));
  LED led_158 (.in(matrixcontroller_1_row9[9]));
  LED led_159 (.in(matrixcontroller_1_row8[10]));
  LED led_160 (.in(matrixcontroller_1_row8[9]));
  LED led_161 (.in(matrixcontroller_1_row7[10]));
  LED led_162 (.in(matrixcontroller_1_row7[9]));
  LED led_163 (.in(matrixcontroller_1_row6[10]));
  LED led_164 (.in(matrixcontroller_1_row6[9]));
  LED led_165 (.in(matrixcontroller_1_row5[10]));
  LED led_166 (.in(matrixcontroller_1_row5[9]));
  LED led_167 (.in(matrixcontroller_1_row4[10]));
  LED led_168 (.in(matrixcontroller_1_row4[9]));
  LED led_169 (.in(matrixcontroller_1_row3[10]));
  LED led_170 (.in(matrixcontroller_1_row3[9]));
  LED led_171 (.in(matrixcontroller_1_row2[10]));
  LED led_172 (.in(matrixcontroller_1_row2[9]));
  LED led_173 (.in(matrixcontroller_1_row1[10]));
  LED led_174 (.in(matrixcontroller_1_row1[9]));
  LED led_175 (.in(matrixcontroller_1_row0[10]));
  LED led_176 (.in(matrixcontroller_1_row0[9]));
  LED led_177 (.in(matrixcontroller_1_row15[11]));
  LED led_178 (.in(matrixcontroller_1_row15[12]));
  LED led_179 (.in(matrixcontroller_1_row14[11]));
  LED led_180 (.in(matrixcontroller_1_row14[12]));
  LED led_181 (.in(matrixcontroller_1_row13[11]));
  LED led_182 (.in(matrixcontroller_1_row13[12]));
  LED led_183 (.in(matrixcontroller_1_row12[11]));
  LED led_184 (.in(matrixcontroller_1_row12[12]));
  LED led_185 (.in(matrixcontroller_1_row11[11]));
  LED led_186 (.in(matrixcontroller_1_row11[12]));
  LED led_187 (.in(matrixcontroller_1_row10[11]));
  LED led_188 (.in(matrixcontroller_1_row10[12]));
  LED led_189 (.in(matrixcontroller_1_row9[11]));
  LED led_190 (.in(matrixcontroller_1_row9[12]));
  LED led_191 (.in(matrixcontroller_1_row8[11]));
  LED led_192 (.in(matrixcontroller_1_row8[12]));
  LED led_193 (.in(matrixcontroller_1_row7[11]));
  LED led_194 (.in(matrixcontroller_1_row7[12]));
  LED led_195 (.in(matrixcontroller_1_row6[11]));
  LED led_196 (.in(matrixcontroller_1_row6[12]));
  LED led_197 (.in(matrixcontroller_1_row5[11]));
  LED led_198 (.in(matrixcontroller_1_row5[12]));
  LED led_199 (.in(matrixcontroller_1_row4[11]));
  LED led_200 (.in(matrixcontroller_1_row4[12]));
  LED led_201 (.in(matrixcontroller_1_row3[11]));
  LED led_202 (.in(matrixcontroller_1_row3[12]));
  LED led_203 (.in(matrixcontroller_1_row2[11]));
  LED led_204 (.in(matrixcontroller_1_row2[12]));
  LED led_205 (.in(matrixcontroller_1_row1[11]));
  LED led_206 (.in(matrixcontroller_1_row1[12]));
  LED led_207 (.in(matrixcontroller_1_row0[11]));
  LED led_208 (.in(matrixcontroller_1_row0[12]));
  LED led_209 (.in(matrixcontroller_1_row15[14]));
  LED led_210 (.in(matrixcontroller_1_row15[13]));
  LED led_211 (.in(matrixcontroller_1_row14[14]));
  LED led_212 (.in(matrixcontroller_1_row14[13]));
  LED led_213 (.in(matrixcontroller_1_row13[14]));
  LED led_214 (.in(matrixcontroller_1_row13[13]));
  LED led_215 (.in(matrixcontroller_1_row12[14]));
  LED led_216 (.in(matrixcontroller_1_row12[13]));
  LED led_217 (.in(matrixcontroller_1_row11[14]));
  LED led_218 (.in(matrixcontroller_1_row11[13]));
  LED led_219 (.in(matrixcontroller_1_row10[14]));
  LED led_220 (.in(matrixcontroller_1_row10[13]));
  LED led_221 (.in(matrixcontroller_1_row9[14]));
  LED led_222 (.in(matrixcontroller_1_row9[13]));
  LED led_223 (.in(matrixcontroller_1_row8[14]));
  LED led_224 (.in(matrixcontroller_1_row8[13]));
  LED led_225 (.in(matrixcontroller_1_row7[14]));
  LED led_226 (.in(matrixcontroller_1_row7[13]));
  LED led_227 (.in(matrixcontroller_1_row6[14]));
  LED led_228 (.in(matrixcontroller_1_row6[13]));
  LED led_229 (.in(matrixcontroller_1_row5[14]));
  LED led_230 (.in(matrixcontroller_1_row5[13]));
  LED led_231 (.in(matrixcontroller_1_row4[14]));
  LED led_232 (.in(matrixcontroller_1_row4[13]));
  LED led_233 (.in(matrixcontroller_1_row3[14]));
  LED led_234 (.in(matrixcontroller_1_row3[13]));
  LED led_235 (.in(matrixcontroller_1_row2[14]));
  LED led_236 (.in(matrixcontroller_1_row2[13]));
  LED led_237 (.in(matrixcontroller_1_row1[14]));
  LED led_238 (.in(matrixcontroller_1_row1[13]));
  LED led_239 (.in(matrixcontroller_1_row0[14]));
  LED led_240 (.in(matrixcontroller_1_row0[13]));
  LED led_241 (.in(matrixcontroller_1_row15[15]));
  LED led_242 (.in(matrixcontroller_1_row14[15]));
  LED led_243 (.in(matrixcontroller_1_row13[15]));
  LED led_244 (.in(matrixcontroller_1_row12[15]));
  LED led_245 (.in(matrixcontroller_1_row11[15]));
  LED led_246 (.in(matrixcontroller_1_row10[15]));
  LED led_247 (.in(matrixcontroller_1_row9[15]));
  LED led_248 (.in(matrixcontroller_1_row8[15]));
  LED led_249 (.in(matrixcontroller_1_row7[15]));
  LED led_250 (.in(matrixcontroller_1_row6[15]));
  LED led_251 (.in(matrixcontroller_1_row5[15]));
  LED led_252 (.in(matrixcontroller_1_row4[15]));
  LED led_253 (.in(matrixcontroller_1_row3[15]));
  LED led_254 (.in(matrixcontroller_1_row2[15]));
  LED led_255 (.in(matrixcontroller_1_row1[15]));
  LED led_256 (.in(matrixcontroller_1_row0[15]));

  // Other names for the same wires on the sheet: In_SrcDest = Addr_Step; In_Temp = Addr_Src; NextInstr = Addr_Src;
  //   In_Dev = Addr_Dest; Out_Temp = Addr_Dest

  // Notes on the sheet:
  //   _8Hz: Hz: 8
  //   _100Hz: Hz: 100
  //   _8Hz_2: Hz: 8
  //   Control changes on -Clk
  //   Data changes on +Clk
  //   Clock Generation
  //   ROM / RAM
  //   0x0000-0x3FFF : ROM
  //   0x4000-0x7FFF : RAM
  //   0xF000-0xF00A : ALU A, B,
  //   SUM, DIF, LSH, RSH, AND, OR,
  //   XOR, NOT, GT, GTE, LT, LTE
  //   0xF100 : Display A
  //   0xF101 : Display B
  //   0xF200 : Matrix Index
  //   0xF201 : Matrix Row
  //   0xFFF0 : Clock Mode
  //   0xFFFF : Step
  //   rom_1 loads program.bin
  //   Hex Displays
  //   Dot Matrix
  //   ALU
  //   contents of Addr_Match (hex, n*v repeats v):
  //   61440*0,1,2,4,8,10,20,40,80,100,200,400,800,1000,2000
endmodule
