// Digital circuit MatrixController.dig as structural Verilog
module MatrixController (
  input  Clk,
  input  W_Row,
  input  W_Index,
  input  [15:0] Data,
  output [15:0] Row15,
  output [15:0] Row14,
  output [15:0] Row13,
  output [15:0] Row12,
  output [15:0] Row11,
  output [15:0] Row10,
  output [15:0] Row9,
  output [15:0] Row8,
  output [15:0] Row7,
  output [15:0] Row6,
  output [15:0] Row5,
  output [15:0] Row4,
  output [15:0] Row3,
  output [15:0] Row2,
  output [15:0] Row1,
  output [15:0] Row0,
  output [15:0] RowData,
  output [3:0] Index
);

  wire demultiplexer_1_out_0, demultiplexer_1_out_1, demultiplexer_1_out_2, demultiplexer_1_out_3,
       demultiplexer_1_out_4, demultiplexer_1_out_5, demultiplexer_1_out_6, demultiplexer_1_out_7,
       demultiplexer_1_out_8, demultiplexer_1_out_9, demultiplexer_1_out_10, demultiplexer_1_out_11,
       demultiplexer_1_out_12, demultiplexer_1_out_13, demultiplexer_1_out_14, demultiplexer_1_out_15;

  Register #(.Bits(4)) register_1 (.D(Data[3:0]), .C(Clk), .en(W_Index), .Q(Index));
  Demultiplexer #(.Selector_Bits(4)) demultiplexer_1 (
    .sel(Index), .in(W_Row), .out_0(demultiplexer_1_out_0), .out_1(demultiplexer_1_out_1),
    .out_2(demultiplexer_1_out_2), .out_3(demultiplexer_1_out_3), .out_4(demultiplexer_1_out_4),
    .out_5(demultiplexer_1_out_5), .out_6(demultiplexer_1_out_6), .out_7(demultiplexer_1_out_7),
    .out_8(demultiplexer_1_out_8), .out_9(demultiplexer_1_out_9), .out_10(demultiplexer_1_out_10),
    .out_11(demultiplexer_1_out_11), .out_12(demultiplexer_1_out_12), .out_13(demultiplexer_1_out_13),
    .out_14(demultiplexer_1_out_14), .out_15(demultiplexer_1_out_15));
  Register #(.Bits(16)) register_2 (
    .D({Data[0], Data[1], Data[2], Data[3], Data[4], Data[5], Data[6], Data[7], Data[8], Data[9], Data[10], Data[11], Data[12], Data[13], Data[14], Data[15]}),
    .C(Clk), .en(demultiplexer_1_out_15), .Q(Row15));
  Register #(.Bits(16)) register_3 (
    .D({Data[0], Data[1], Data[2], Data[3], Data[4], Data[5], Data[6], Data[7], Data[8], Data[9], Data[10], Data[11], Data[12], Data[13], Data[14], Data[15]}),
    .C(Clk), .en(demultiplexer_1_out_11), .Q(Row11));
  Register #(.Bits(16)) register_4 (
    .D({Data[0], Data[1], Data[2], Data[3], Data[4], Data[5], Data[6], Data[7], Data[8], Data[9], Data[10], Data[11], Data[12], Data[13], Data[14], Data[15]}),
    .C(Clk), .en(demultiplexer_1_out_7), .Q(Row7));
  Register #(.Bits(16)) register_5 (
    .D({Data[0], Data[1], Data[2], Data[3], Data[4], Data[5], Data[6], Data[7], Data[8], Data[9], Data[10], Data[11], Data[12], Data[13], Data[14], Data[15]}),
    .C(Clk), .en(demultiplexer_1_out_3), .Q(Row3));
  Register #(.Bits(16)) register_6 (
    .D({Data[0], Data[1], Data[2], Data[3], Data[4], Data[5], Data[6], Data[7], Data[8], Data[9], Data[10], Data[11], Data[12], Data[13], Data[14], Data[15]}),
    .C(Clk), .en(demultiplexer_1_out_14), .Q(Row14));
  Register #(.Bits(16)) register_7 (
    .D({Data[0], Data[1], Data[2], Data[3], Data[4], Data[5], Data[6], Data[7], Data[8], Data[9], Data[10], Data[11], Data[12], Data[13], Data[14], Data[15]}),
    .C(Clk), .en(demultiplexer_1_out_10), .Q(Row10));
  Register #(.Bits(16)) register_8 (
    .D({Data[0], Data[1], Data[2], Data[3], Data[4], Data[5], Data[6], Data[7], Data[8], Data[9], Data[10], Data[11], Data[12], Data[13], Data[14], Data[15]}),
    .C(Clk), .en(demultiplexer_1_out_6), .Q(Row6));
  Register #(.Bits(16)) register_9 (
    .D({Data[0], Data[1], Data[2], Data[3], Data[4], Data[5], Data[6], Data[7], Data[8], Data[9], Data[10], Data[11], Data[12], Data[13], Data[14], Data[15]}),
    .C(Clk), .en(demultiplexer_1_out_2), .Q(Row2));
  Register #(.Bits(16)) register_10 (
    .D({Data[0], Data[1], Data[2], Data[3], Data[4], Data[5], Data[6], Data[7], Data[8], Data[9], Data[10], Data[11], Data[12], Data[13], Data[14], Data[15]}),
    .C(Clk), .en(demultiplexer_1_out_13), .Q(Row13));
  Register #(.Bits(16)) register_11 (
    .D({Data[0], Data[1], Data[2], Data[3], Data[4], Data[5], Data[6], Data[7], Data[8], Data[9], Data[10], Data[11], Data[12], Data[13], Data[14], Data[15]}),
    .C(Clk), .en(demultiplexer_1_out_9), .Q(Row9));
  Register #(.Bits(16)) register_12 (
    .D({Data[0], Data[1], Data[2], Data[3], Data[4], Data[5], Data[6], Data[7], Data[8], Data[9], Data[10], Data[11], Data[12], Data[13], Data[14], Data[15]}),
    .C(Clk), .en(demultiplexer_1_out_5), .Q(Row5));
  Register #(.Bits(16)) register_13 (
    .D({Data[0], Data[1], Data[2], Data[3], Data[4], Data[5], Data[6], Data[7], Data[8], Data[9], Data[10], Data[11], Data[12], Data[13], Data[14], Data[15]}),
    .C(Clk), .en(demultiplexer_1_out_1), .Q(Row1));
  Register #(.Bits(16)) register_14 (
    .D({Data[0], Data[1], Data[2], Data[3], Data[4], Data[5], Data[6], Data[7], Data[8], Data[9], Data[10], Data[11], Data[12], Data[13], Data[14], Data[15]}),
    .C(Clk), .en(demultiplexer_1_out_12), .Q(Row12));
  Register #(.Bits(16)) register_15 (
    .D({Data[0], Data[1], Data[2], Data[3], Data[4], Data[5], Data[6], Data[7], Data[8], Data[9], Data[10], Data[11], Data[12], Data[13], Data[14], Data[15]}),
    .C(Clk), .en(demultiplexer_1_out_8), .Q(Row8));
  Register #(.Bits(16)) register_16 (
    .D({Data[0], Data[1], Data[2], Data[3], Data[4], Data[5], Data[6], Data[7], Data[8], Data[9], Data[10], Data[11], Data[12], Data[13], Data[14], Data[15]}),
    .C(Clk), .en(demultiplexer_1_out_4), .Q(Row4));
  Register #(.Bits(16)) register_17 (
    .D({Data[0], Data[1], Data[2], Data[3], Data[4], Data[5], Data[6], Data[7], Data[8], Data[9], Data[10], Data[11], Data[12], Data[13], Data[14], Data[15]}),
    .C(Clk), .en(demultiplexer_1_out_0), .Q(Row0));
  Multiplexer #(.Selector_Bits(4), .Bits(16)) multiplexer_1 (
    .sel(Index), .in_0(Row0), .in_1(Row1), .in_2(Row2), .in_3(Row3), .in_4(Row4), .in_5(Row5), .in_6(Row6),
    .in_7(Row7), .in_8(Row8), .in_9(Row9), .in_10(Row10), .in_11(Row11), .in_12(Row12), .in_13(Row13),
    .in_14(Row14), .in_15(Row15), .out(RowData));

  // Other names for the same wires on the sheet: D[15:0] = {Data[0], Data[1], Data[2], Data[3], Data[4], Data[5], Data[6], Data[7], Data[8], Data[9], Data[10], Data[11], Data[12], Data[13], Data[14], Data[15]}
endmodule
