// Digital circuit RangeDeviceSelector.dig as structural Verilog
module RangeDeviceSelector (
  input  [15:0] Addr_Upper,
  input  [15:0] Addr_Lower,
  input  [15:0] Addr,
  input  In_Dev,
  input  Out_Dev,
  output In,
  output Out
);

  wire and_1_out, comparator_1_eq, comparator_1_gt, comparator_2_eq, comparator_2_lt, or_1_out, or_2_out;

  Comparator #(.Bits(16)) comparator_1 (
    .a(Addr_Upper), .b(Addr), .gt(comparator_1_gt), .eq(comparator_1_eq));  // open: lt
  Comparator #(.Bits(16)) comparator_2 (
    .a(Addr_Lower), .b(Addr), .eq(comparator_2_eq), .lt(comparator_2_lt));  // open: gt
  or or_1 (or_1_out, comparator_1_gt, comparator_1_eq);
  or or_2 (or_2_out, comparator_2_eq, comparator_2_lt);
  and and_1 (and_1_out, or_1_out, or_2_out);
  and and_2 (In, In_Dev, and_1_out);
  and and_3 (Out, and_1_out, Out_Dev);
endmodule
