// Digital circuit ResetTimer.dig as structural Verilog
// Ensures correct timing of the reset signal.
// Requires this sequence of high signals: ~Clk, Clk, ~Clk
module ResetTimer (
  input  Rst_Raw,
  input  Clk,
  input  nClk,
  output Rst,
  output nRst
);

  wire and_1_out, and_2_out, and_3_out, rs_ff_as_2_q, rs_ff_as_3_q;

  RS_FF_AS rs_ff_as_1 (.S(Rst_Raw), .R(and_3_out), .Q(Rst), .nQ(nRst));
  and and_1 (and_1_out, Rst, nClk);
  RS_FF_AS rs_ff_as_2 (.S(and_1_out), .R(and_3_out), .Q(rs_ff_as_2_q));  // open: nQ
  and and_2 (and_2_out, rs_ff_as_2_q, Clk);
  RS_FF_AS rs_ff_as_3 (.S(and_2_out), .R(and_3_out), .Q(rs_ff_as_3_q));  // open: nQ
  and and_3 (and_3_out, rs_ff_as_3_q, nClk);
endmodule
